// Logisim project assign1.circ as structural Verilog: 1 circuit, main circuit main
module main (
  input  PlayPause
);

  wire clock_1_out, d_ff_1_q, d_ff_1_qn;

  Clock clock_1 (.out(clock_1_out));
  D_Flip_Flop d_ff_1 (.D(PlayPause), .clk(clock_1_out), .Q(d_ff_1_q), .Qn(d_ff_1_qn));  // open: preset, reset
  LED Playing (.in(d_ff_1_q));
  LED Paused (.in(d_ff_1_qn));
endmodule
